# Fritzing sketch breadboard (saved by Fritzing 0.9.3b)
breadboards: 1

parts:
  VCC1 = Battery block 9V
  R1 = Resistor [tolerance=±5% resistance=10k package="0603 [SMD]"]
  R2 = Photocell (LDR) [package=THT]
  Q1 = PNP-Transistor [package="SOT-23 [SMD]"]
  R3 = Resistor [tolerance=±5% resistance=2.2k package="0603 [SMD]"]
  R4 = Resistor [tolerance=±5% resistance=330k package="0603 [SMD]"]
  LED1 = LED - 3mm [color="Red (633nm)" package="3 mm [THT]"]

nets:
  N1: VCC1.-, R4.Pin_1, LED1.cathode
  N2: VCC1.+, R1.Pin_0, Q1.2
  N3: R1.Pin_1, R2.pin_0
  N4: R2.pin_1, Q1.0, R4.Pin_0
  N5: Q1.1, R3.Pin_0
  N6: R3.Pin_1, LED1.anode
