# Fritzing sketch schematic (saved by Fritzing 0.9.3b)
breadboards: 1

parts:
  R3 = Resistor [tolerance=±5% resistance=2.2k package="2512 [SMD]"]
  LED1 = smd LED [color="Blue (430nm)" package="0603 [SMD]"]
  LDR = Photocell (LDR) [package=THT]
  R1 = Resistor [tolerance=±5% resistance=10k package="2512 [SMD]"]
  R2 = Resistor [tolerance=±5% resistance=330k package="2512 [SMD]"]
  PNP_-_BC327 = PNP-Transistor [package="TO92 [THT]"]

nets:
  N1: R3.Pin_0, PNP_-_BC327.E
  N2: R3.Pin_1, LED1.anode
  GND: LED1.cathode, R2.Pin_0
  N3: LDR.pin_0, R1.Pin_1
  N4: LDR.pin_1, R2.Pin_1, PNP_-_BC327.B
  9V: R1.Pin_0, PNP_-_BC327.C
